# Fritzing sketch sketch (saved by Fritzing 0.9.3b)
breadboards: 1

parts:
  Pro_Micro1 = Pro Micro
  LED1 = smd LED [color="Red (633nm)" package="0603 [SMD]"]
  LED2 = smd LED [color="Red (633nm)" package="0603 [SMD]"]
  LED3 = smd LED [color="Yellow (585nm)" package="0603 [SMD]"]
  LED4 = smd LED [color="Yellow (585nm)" package="0603 [SMD]"]
  LED5 = smd LED [color="Yellow (585nm)" package="0603 [SMD]"]
  LED6 = smd LED [color="Green (555nm)" package="0603 [SMD]"]
  LED7 = smd LED [color="Yellow (585nm)" package="0603 [SMD]"]
  LED8 = smd LED [color="Green (555nm)" package="0603 [SMD]"]
  LED9 = smd LED [color="Green (555nm)" package="0603 [SMD]"]
  R1 = Resistor [tolerance=±5% resistance=1k package=THT]
  R2 = Resistor [tolerance=±5% resistance=1k package=THT]
  R3 = Resistor [tolerance=±5% resistance=1k package=THT]
  R4 = Resistor [tolerance=±5% resistance=1k package=THT]
  R5 = Resistor [tolerance=±5% resistance=1k package=THT]
  R6 = Resistor [tolerance=±5% resistance=1k package=THT]
  R8 = Resistor [tolerance=±5% resistance=1k package=THT]
  R9 = Resistor [tolerance=±5% resistance=1k package=THT]
  R10 = Resistor [tolerance=±5% resistance=1k package=THT]
  R11 = Resistor [tolerance=±5% resistance=10k package="0805 [SMD]"]
  S4 = Momentary Switch [package=ksa_sealed_tac_switch]
  LED10 = smd LED [color="Red (633nm)" package="0603 [SMD]"]
  LED11 = smd LED [color="Red (633nm)" package="0603 [SMD]"]
  R12 = Resistor [tolerance=±5% resistance=1k package=THT]
  R13 = Resistor [tolerance=±5% resistance=1k package=THT]
  S5 = Momentary Switch [package=ksa_sealed_tac_switch]
  R14 = Resistor [tolerance=±5% resistance=10k package="0805 [SMD]"]
  MPX4250AP1 = MPX4250AP pressure sensor [part_number=MPX]

nets:
  N1: Pro_Micro1.TX1, S5.1
  N2: Pro_Micro1.RX0, S4.1
  N3: Pro_Micro1.D2, R9.Pin_1
  N4: Pro_Micro1.D3, R8.Pin_1
  N5: Pro_Micro1.D4, R10.Pin_1
  N6: Pro_Micro1.D5, R5.Pin_1
  N7: Pro_Micro1.D6, R6.Pin_1
  N8: Pro_Micro1.D7, R1.Pin_1
  N9: Pro_Micro1.D8, R2.Pin_1
  N10: Pro_Micro1.D9, R3.Pin_1
  N11: Pro_Micro1.D10, R4.Pin_1
  N12: Pro_Micro1.D16/MOSI, R13.Pin_1
  N13: Pro_Micro1.D14/MISO, R12.Pin_1
  N14: Pro_Micro1.D18/A0, MPX4250AP1.V_out
  N15: Pro_Micro1.VCC, S4.4, S5.4, MPX4250AP1.Vs
  GND: Pro_Micro1.GND, LED1.cathode, LED2.cathode, LED3.cathode, LED4.cathode, LED5.cathode, LED6.cathode, LED8.cathode, LED9.cathode, R11.Pin_1, LED10.cathode, LED11.cathode, R14.Pin_1, MPX4250AP1.GND
  N16: LED1.anode, R9.Pin_0
  N17: LED2.anode, R8.Pin_0
  N18: LED3.anode, R3.Pin_0
  N19: LED4.anode, R4.Pin_0
  N20: LED5.anode, R10.Pin_0
  N21: LED6.anode, R2.Pin_0
  N22: LED7.anode, R5.Pin_0
  N23: LED8.anode, R1.Pin_0
  N24: LED9.anode, R6.Pin_0
  N25: R11.Pin_0, S5.2
  N26: S4.2, R14.Pin_0
  N27: LED10.anode, R13.Pin_0
  N28: LED11.anode, R12.Pin_0

custom parts:
  Pro Micro: The SparkFun Pro Micro is a complete USB-based microcontoller development system, in a very small footprint, capable of implementing many types of projects. All programming can be done via the USB port.
